// Logisim project bin_converter.circ as structural Verilog: 2 circuits, main circuit bin_converter
module bin_converter (
  input  [2:0] ABC,
  output O6,
  output O5,
  output O4,
  output O3,
  output O2,
  output O1,
  output O0
);

  wire and_3_out, and_4_out, and_5_out;

  and and_1 (O6, ABC[2], ABC[1], ABC[0]);
  and and_2 (O5, ABC[2], ABC[1]);
  and and_3 (and_3_out, ABC[2], ABC[0]);
  and and_4 (and_4_out, ABC[2], ABC[1]);
  and and_5 (and_5_out, ABC[1], ABC[0]);
  or or_1 (O1, ABC[1], ABC[2]);
  or or_2 (O0, ABC[0], ABC[1], ABC[2]);
  or or_3 (O4, and_3_out, and_4_out);
  or or_4 (O2, and_5_out, ABC[2]);

  assign O3 = ABC[2];

  // Notes on the sheet:
  //   Timmy Do
  //   Lab OLA3
  //   bin_converter
endmodule

module display (
  input  [2:0] ABC
);

  wire bin_converter_1_o0, bin_converter_1_o1, bin_converter_1_o2, bin_converter_1_o3, bin_converter_1_o4,
       bin_converter_1_o5, bin_converter_1_o6;

  bin_converter bin_converter_1 (
    .ABC(ABC), .O6(bin_converter_1_o6), .O5(bin_converter_1_o5), .O4(bin_converter_1_o4),
    .O3(bin_converter_1_o3), .O2(bin_converter_1_o2), .O1(bin_converter_1_o1), .O0(bin_converter_1_o0));
  LED led_1 (.in(bin_converter_1_o6));
  LED led_2 (.in(bin_converter_1_o5));
  LED led_3 (.in(bin_converter_1_o4));
  LED led_4 (.in(bin_converter_1_o3));
  LED led_5 (.in(bin_converter_1_o2));
  LED led_6 (.in(bin_converter_1_o1));
  LED led_7 (.in(bin_converter_1_o0));

  // Notes on the sheet:
  //   Timmy Do
  //   Lab OLA3
  //   display
endmodule
