// Logisim project homework5.circ as structural Verilog: 2 circuits, main circuit Display
module count (
  input  R,
  input  Clock,
  output [1:0] Out2Bit
);

  wire and_1_out, not_1_out, or_1_out;

  and and_1 (and_1_out, not_1_out, Out2Bit[0]);
  or or_1 (or_1_out, Out2Bit[0], R);
  J_K_Flip_Flop A (.J(and_1_out), .clk(Clock), .K(or_1_out), .Q(Out2Bit[1]), .en(1'b1));  // open: Qn, preset, reset
  not not_1 (not_1_out, R);
  J_K_Flip_Flop B (.J(not_1_out), .clk(Clock), .K(1'b1), .Q(Out2Bit[0]), .en(1'b1));  // open: Qn, preset, reset
endmodule

module Display (
  input  R
);

  wire clock_1_out, n7segdecoder_1_p3, n7segdecoder_1_p4, n7segdecoder_1_p5, n7segdecoder_1_p6,
       n7segdecoder_1_p7, n7segdecoder_1_p8, n7segdecoder_1_p9, n7segdecoder_1_p10;
  wire [1:0] count_1_out2bit;

  Clock clock_1 (.out(clock_1_out));
  count count_1 (.R(R), .Clock(clock_1_out), .Out2Bit(count_1_out2bit));
  // _7segDecoder 7segdecoder_1: pin names not known; wires that end beside it: count_1_out2bit, 1'b0, n7segdecoder_1_p3, n7segdecoder_1_p4, n7segdecoder_1_p5, n7segdecoder_1_p6, n7segdecoder_1_p7, n7segdecoder_1_p8, n7segdecoder_1_p9, n7segdecoder_1_p10
  _7_Segment_Display u_7_segment_display_1 (
    .g(n7segdecoder_1_p9), .f(n7segdecoder_1_p8), .a(n7segdecoder_1_p3), .b(n7segdecoder_1_p4),
    .e(n7segdecoder_1_p7), .d(n7segdecoder_1_p6), .c(n7segdecoder_1_p5), .dp(n7segdecoder_1_p10));
endmodule
