// Logisim project mod_counter.circ as structural Verilog: 2 circuits, main circuit Mod9
module Mod9 (
  input  Clock,
  output [3:0] Output
);

  wire A_qn, and_1_out, and_2_out, and_3_out, B_qn, C_qn, D_qn, or_1_out;

  and and_1 (and_1_out, B_qn, Output[1], Output[0]);
  J_K_Flip_Flop A (.J(and_1_out), .clk(Clock), .K(1'b1), .Q(Output[3]), .Qn(A_qn), .en(1'b1));  // open: preset, reset
  or or_1 (or_1_out, C_qn, D_qn);
  J_K_Flip_Flop B (.J(or_1_out), .clk(Clock), .K(1'b1), .Q(Output[2]), .Qn(B_qn), .en(1'b1));  // open: preset, reset
  and and_2 (and_2_out, Output[0], B_qn);
  J_K_Flip_Flop C (
    .J(and_2_out), .clk(Clock), .K(and_2_out), .Q(Output[1]), .Qn(C_qn), .en(1'b1));  // open: preset, reset
  and and_3 (and_3_out, A_qn, B_qn);
  J_K_Flip_Flop D (.J(and_3_out), .clk(Clock), .K(B_qn), .Q(Output[0]), .Qn(D_qn), .en(1'b1));  // open: preset, reset
  // Probe on Output

  // Notes on the sheet:
  //   Timmy Do
  //   Lab # OLA4
  //   Mod9
endmodule

module Display (
);

  wire _7_Seg_dp_out, _7_Seg_pld_a, _7_Seg_pld_b, _7_Seg_pld_c, _7_Seg_pld_d, _7_Seg_pld_e, _7_Seg_pld_f,
       _7_Seg_pld_g, clock_1_out;
  wire [3:0] Mod9_output;

  Clock clock_1 (.out(clock_1_out));
  Mod9 Mod9 (.Clock(clock_1_out), .Output(Mod9_output));
  _7segDecoder _7_Seg (
    .BCD_IN(Mod9_output), .DP_IN(1'b0), .PLD_a(_7_Seg_pld_a), .PLD_b(_7_Seg_pld_b), .PLD_c(_7_Seg_pld_c),
    .PLD_d(_7_Seg_pld_d), .PLD_e(_7_Seg_pld_e), .PLD_f(_7_Seg_pld_f), .PLD_g(_7_Seg_pld_g),
    .DP_OUT(_7_Seg_dp_out));
  _7_Segment_Display u_7_segment_display_1 (
    .g(_7_Seg_pld_g), .f(_7_Seg_pld_f), .a(_7_Seg_pld_a), .b(_7_Seg_pld_b), .e(_7_Seg_pld_e),
    .d(_7_Seg_pld_d), .c(_7_Seg_pld_c), .dp(_7_Seg_dp_out));

  // Notes on the sheet:
  //   Timmy Do
  //   Lab # OLA4
  //   Display
endmodule
